# Fritzing sketch encoder_led_example (saved by Fritzing 0.9.3b)

parts:
  Part1 = Arduino Uno (Rev3)
  U1 = ENCODER-QUADRATURE [package=encoder-16mm-quad]
  Part2 = ws2812b [package="smd 2812b"]
  S1 = Square Pushbutton
  Part3 = ws2812b [package="smd 2812b"]
  Part4 = ws2812b [package="smd 2812b"]

nets:
  N1: Part1.D8, Part2.DIN
  VSS: Part1.GND, U1.B, Part2.VSS, S1.leg1, Part3.VSS, Part4.VSS
  N2: Part1.D2, U1.A
  N3: Part1.D3_PWM, U1.C
  N4: Part1.D4, S1.leg0
  VDD: Part1.VIN, Part2.VDD, Part3.VDD, Part4.VDD
  N5: Part2.DOUT, Part3.DIN
  N6: Part3.DOUT, Part4.DIN
